// Logisim project aiAlu.circ as structural Verilog: 9 circuits, main circuit Half Adder
module Half_Adder (
  input  A,
  input  B,
  output S,
  output C
);

  xor xor_1 (S, A, B);
  and and_1 (C, A, B);
endmodule

module Full_Adder (
  input  C0,
  input  A,
  input  B,
  output S,
  output C1
);

  wire and_1_out, and_2_out, and_3_out, xor_1_out;

  xor xor_1 (xor_1_out, B, A);
  xor xor_2 (S, xor_1_out, C0);
  and and_1 (and_1_out, A, C0);
  and and_2 (and_2_out, B, A);
  and and_3 (and_3_out, B, C0);
  or or_1 (C1, and_1_out, and_2_out, and_3_out);
endmodule

module aiLogic (
  input  [7:0] in_1,
  input  [7:0] in_2
);
endmodule

module a_b (
  input  [7:0] in_1,
  input  [7:0] in_2,
  output [7:0] out_3
);

  and and_1 (out_3[7], in_2[7], in_1[7]);
  and and_2 (out_3[6], in_2[6], in_1[6]);
  and and_3 (out_3[5], in_2[5], in_1[5]);
  and and_4 (out_3[4], in_2[4], in_1[4]);
  and and_5 (out_3[2], in_2[2], in_1[2]);
  and and_6 (out_3[3], in_2[3], in_1[3]);
  and and_7 (out_3[1], in_2[1], in_1[1]);
  and and_8 (out_3[0], in_2[0], in_1[0]);
endmodule

module a__b (
  input  [7:0] in_1,
  input  [7:0] in_2,
  output [7:0] out_3
);

  or or_1 (out_3[7], in_2[7], in_1[7]);
  or or_2 (out_3[5], in_2[5], in_1[5]);
  or or_3 (out_3[4], in_2[4], in_1[4]);
  or or_4 (out_3[6], in_2[6], in_1[6]);
  or or_5 (out_3[2], in_2[2], in_1[2]);
  or or_6 (out_3[3], in_2[3], in_1[3]);
  or or_7 (out_3[1], in_2[1], in_1[1]);
  or or_8 (out_3[0], in_2[0], in_1[0]);
endmodule

module adder_8_bit_extended (
  input  [7:0] A,
  input  [7:0] B,
  output [7:0] adder_8_bit,
  output carry
);

  wire c, full_adder_1_c1, full_adder_2_c1, full_adder_4_c1, full_adder_5_c1, full_adder_6_c1, half_adder_1_c;

  Half_Adder half_adder_1 (.S(A[7]), .C(half_adder_1_c), .A(A[0]), .B(B[0]));
  Full_Adder full_adder_1 (.S(adder_8_bit[1]), .C1(full_adder_1_c1), .C0(half_adder_1_c), .A(A[1]), .B(B[1]));
  Full_Adder full_adder_2 (.S(A[7]), .C1(full_adder_2_c1), .C0(full_adder_1_c1), .A(A[2]), .B(B[2]));
  Full_Adder full_adder_3 (.S(adder_8_bit[3]), .C1(c), .C0(full_adder_2_c1), .A(A[3]), .B(B[3]));
  Full_Adder full_adder_4 (.S(adder_8_bit[4]), .C1(full_adder_4_c1), .C0(c), .A(A[4]), .B(B[4]));
  Full_Adder full_adder_5 (.S(adder_8_bit[5]), .C1(full_adder_5_c1), .C0(full_adder_4_c1), .A(A[5]), .B(B[5]));
  Full_Adder full_adder_6 (.S(adder_8_bit[6]), .C1(full_adder_6_c1), .C0(full_adder_5_c1), .A(A[6]), .B(B[6]));
  Full_Adder full_adder_7 (.S(adder_8_bit[7]), .C1(carry), .C0(full_adder_6_c1), .A(A[7]), .B(B[7]));

  assign {adder_8_bit[2], adder_8_bit[0]} = {2{A[7]}};

  // Other names for the same wires on the sheet: s1 = adder_8_bit[1]; s0 = A[7]; s2 = A[7]; s3 = adder_8_bit[3];
  //   s4 = adder_8_bit[4]; s5 = adder_8_bit[5]; s6 = adder_8_bit[6]; s7 = adder_8_bit[7]
endmodule

module half_subtract (
  input  A,
  input  B,
  output Y,
  output b1
);

  wire not_1_out;

  xor xor_1 (Y, B, A);
  not not_1 (not_1_out, A);
  and and_1 (b1, not_1_out, B);
endmodule

module full_subtract (
  input  b0,
  input  A,
  input  B,
  output Y,
  output b1
);

  wire and_1_out, and_2_out, not_1_out, xor_1_out;

  not not_1 (not_1_out, A);
  xor xor_1 (xor_1_out, B, A);
  and and_1 (and_1_out, B, not_1_out);
  xor xor_2 (Y, xor_1_out, b0);
  and and_2 (and_2_out, xor_1_out, b0);
  or or_1 (b1, and_1_out, and_2_out);
endmodule

module subtract_8_bit__extended (
  input  [7:0] A,
  input  [7:0] B,
  output B_2,
  output [7:0] subtractor_8_bit
);

  wire b_t, full_subtract_1_b1, full_subtract_2_b1, full_subtract_4_b1, full_subtract_5_b1,
       full_subtract_6_b1, half_subtract_1_b1;

  half_subtract half_subtract_1 (.Y(subtractor_8_bit[0]), .b1(half_subtract_1_b1), .A(A[0]), .B(B[0]));
  full_subtract full_subtract_1 (.Y(subtractor_8_bit[6]), .b1(full_subtract_1_b1), .b0(b_t), .A(A[6]), .B(B[6]));
  full_subtract full_subtract_2 (
    .Y(subtractor_8_bit[1]), .b1(full_subtract_2_b1), .b0(half_subtract_1_b1), .A(A[1]), .B(B[1]));
  full_subtract full_subtract_3 (.Y(subtractor_8_bit[7]), .b1(B_2), .b0(full_subtract_1_b1), .A(A[7]), .B(B[7]));
  full_subtract full_subtract_4 (
    .Y(subtractor_8_bit[2]), .b1(full_subtract_4_b1), .b0(full_subtract_2_b1), .A(A[2]), .B(B[2]));
  full_subtract full_subtract_5 (
    .Y(subtractor_8_bit[3]), .b1(full_subtract_5_b1), .b0(full_subtract_4_b1), .A(A[3]), .B(B[3]));
  full_subtract full_subtract_6 (
    .Y(subtractor_8_bit[4]), .b1(full_subtract_6_b1), .b0(full_subtract_5_b1), .A(A[4]), .B(B[4]));
  full_subtract full_subtract_7 (.Y(subtractor_8_bit[5]), .b1(b_t), .b0(full_subtract_6_b1), .A(A[5]), .B(B[5]));

  // Other names for the same wires on the sheet: _6a = A[6]; _7a = A[7]; _6b = B[6]; _7b = B[7];
  //   _0 = subtractor_8_bit[0]; _1 = subtractor_8_bit[1]; _2 = subtractor_8_bit[2]; _3 = subtractor_8_bit[3];
  //   _4 = subtractor_8_bit[4]; _5 = subtractor_8_bit[5]; _6 = subtractor_8_bit[6]; _7 = subtractor_8_bit[7]
endmodule
